// Logisim project cpu.circ as structural Verilog: 1 circuit, main circuit CPU
module CPU (
  input  [31:0] Instruction,
  input  CLK,
  output [31:0] s0,
  output [31:0] s1,
  output [31:0] t0,
  output [31:0] t1,
  output [31:0] a0,
  output [31:0] ra,
  output [31:0] sp,
  output [31:0] PC
);

  wire pc_1_p1;

  // PC pc_1: pin names not known; wires that end beside it: pc_1_p1, CLK, PC
  // Incrementer incrementer_1: pin names not known; wires that end beside it: PC, pc_1_p1
  RegFile regfile_1 (
    .Clk(CLK), .s0(s0), .s1(s1), .t0(t0), .t1(t1), .a0(a0), .ra(ra), .sp(sp));  // open: R1, R2, WE, W, RD, RS1, RS2
  // ALU alu_1: pin names not known
  // memory_main main_1: pin names not known

  // Other names for the same wires on the sheet: fetch_addr[31:0] = PC; INST[31:0] = Instruction

  // Notes on the sheet:
  //   NOTE
  //   Please do not modify/replace/move/change/delete/etc input and output pins
  //   These are debug/test outputs from your circuit
endmodule
