// Logisim project regfile.circ as structural Verilog: 1 circuit, main circuit RegFile
module RegFile (
  input  [4:0] RD,
  input  [4:0] RS1,
  input  [4:0] RS2,
  input  [31:0] W,
  input  WE,
  input  Clk,
  output [31:0] s0,
  output [31:0] s1,
  output [31:0] t0,
  output [31:0] t1,
  output [31:0] a0,
  output [31:0] ra,
  output [31:0] sp,
  output [31:0] R1,
  output [31:0] R2
);

  wire and_1_out, and_2_out, and_3_out, and_4_out, and_5_out, and_6_out, and_7_out, and_8_out, and_9_out,
       demultiplexer_1_out0, demultiplexer_1_out1, demultiplexer_1_out2, demultiplexer_1_out5,
       demultiplexer_1_out6, demultiplexer_1_out8, demultiplexer_1_out9, demultiplexer_1_out10,
       demultiplexer_1_out11;
  wire [31:0] register_1_q, register_9_q;

  Demultiplexer #(.select(5)) demultiplexer_1 (
    .out0(demultiplexer_1_out0), .out1(demultiplexer_1_out1), .out2(demultiplexer_1_out2),
    .out5(demultiplexer_1_out5), .out6(demultiplexer_1_out6), .out8(demultiplexer_1_out8),
    .out9(demultiplexer_1_out9), .out10(demultiplexer_1_out10), .out11(demultiplexer_1_out11), .sel(RD));  // open: out3, out4, out7, out12, out13, out14, out15, out16, out17, out18, out19, out20, out21, out22, out23, out24, out25, out26, out27, out28, out29, out30, out31, in, en
  and and_1 (and_1_out, demultiplexer_1_out0, WE);
  and and_2 (and_2_out, demultiplexer_1_out1, WE);
  and and_3 (and_3_out, demultiplexer_1_out2, WE);
  and and_4 (and_4_out, demultiplexer_1_out5, WE);
  and and_5 (and_5_out, demultiplexer_1_out6, WE);
  and and_6 (and_6_out, demultiplexer_1_out8, WE);
  and and_7 (and_7_out, demultiplexer_1_out9, WE);
  and and_8 (and_8_out, demultiplexer_1_out10, WE);
  and and_9 (and_9_out, demultiplexer_1_out11, WE);
  Register #(.width(32)) register_1 (.Q(register_1_q), .clk(Clk), .clr(and_1_out));  // open: D, en
  Register #(.width(32)) register_2 (.D(W), .Q(ra), .clk(Clk), .clr(and_2_out));  // open: en
  Register #(.width(32)) register_3 (.D(W), .Q(sp), .clk(Clk), .clr(and_3_out));  // open: en
  Register #(.width(32)) register_4 (.D(W), .Q(t0), .clk(Clk), .clr(and_4_out));  // open: en
  Register #(.width(32)) register_5 (.D(W), .Q(t1), .clk(Clk), .clr(and_5_out));  // open: en
  Register #(.width(32)) register_6 (.D(W), .Q(s0), .clk(Clk), .clr(and_6_out));  // open: en
  Register #(.width(32)) register_7 (.D(W), .Q(s1), .clk(Clk), .clr(and_7_out));  // open: en
  Register #(.width(32)) register_8 (.D(W), .Q(a0), .clk(Clk), .clr(and_8_out));  // open: en
  Register #(.width(32)) register_9 (.D(W), .Q(register_9_q), .clk(Clk), .clr(and_9_out));  // open: en
  Multiplexer #(.select(5), .width(32)) multiplexer_1 (
    .in0(register_1_q), .in1(ra), .in2(sp), .in5(t0), .in6(t1), .in8(s0), .in9(s1), .in10(a0),
    .in11(register_9_q), .out(R1), .sel(RS1));  // open: in3, in4, in7, in12, in13, in14, in15, in16, in17, in18, in19, in20, in21, in22, in23, in24, in25, in26, in27, in28, in29, in30, in31, en
  Multiplexer #(.select(5), .width(32)) multiplexer_2 (
    .in0(register_1_q), .in1(ra), .in2(sp), .in5(t0), .in6(t1), .in8(s0), .in9(s1), .in10(a0),
    .in11(register_9_q), .out(R2), .sel(RS2));  // open: in3, in4, in7, in12, in13, in14, in15, in16, in17, in18, in19, in20, in21, in22, in23, in24, in25, in26, in27, in28, in29, in30, in31, en

  // Notes on the sheet:
  //   Write Register
  //   Read Register 1
  //   Read Register 2
  //   Write Data
  //   Write Enable
  //   Clock
  //   NOTE
  //   Please do not modify/replace/move/change/delete/etc input and output pins
  //   These are debug/test outputs from your circuit
  //   Read Data 1
  //   Read Data 2
endmodule
